# Fritzing sketch testout1 (saved by Fritzing 0.9.4)
breadboards: 1

parts:
  power = Battery
  resistor_1 = Resistor [resistance=200 tolerance=±5% package=THT]
  resistor_2 = Resistor [resistance=200 tolerance=±5% package=THT]
  resistor_3 = Resistor [resistance=200 tolerance=±5% package=THT]
  resistor_4 = Resistor [resistance=200 tolerance=±5% package=THT]
  resistor_5 = Resistor [resistance=200 tolerance=±5% package=THT]

nets:
  N1: power.-, resistor_4.Pin_1, resistor_5.Pin_1
  N2: power.+, resistor_1.Pin_0, resistor_2.Pin_0
  N3: resistor_1.Pin_1, resistor_3.Pin_0, resistor_4.Pin_0
  N4: resistor_2.Pin_1, resistor_3.Pin_1, resistor_5.Pin_0
